// Logisim project FastStarter.circ as structural Verilog: 1 circuit, main circuit main
module main (
  input  [3:0] Multiplicand,
  input  [3:0] Multiplier,
  output [3:0] out_3,
  output [3:0] out_4,
  output [3:0] out_5,
  output [3:0] out_6
);

  Multiplier #(.width(4)) multiplier_1 (.a(Multiplicand), .b({3'b000, Multiplier[0]}), .out(out_3));  // open: cin, cout
  Multiplier #(.width(4)) multiplier_2 (.a(Multiplicand), .b({3'b000, Multiplier[1]}), .out(out_4));  // open: cin, cout
  Multiplier #(.width(4)) multiplier_3 (.a(Multiplicand), .b({3'b000, Multiplier[2]}), .out(out_5));  // open: cin, cout
  Multiplier #(.width(4)) multiplier_4 (.a(Multiplicand), .b({3'b000, Multiplier[3]}), .out(out_6));  // open: cin, cout
endmodule
