// Logisim project x86.circ as structural Verilog: 1 circuit, main circuit main
module main (
  output [15:0] Next_Instruction,
  output [7:0] sum,
  output [7:0] lower_bits,
  output MUX_select
);

  wire Clock_out, not_1_out, not_2_out, not_3_out, not_4_out, Reset_out;
  wire [3:0] Ins_Ptr_q;
  wire [7:0] multiplexer_1_out, rax_q;

  Counter #(.width(4), .max('hf)) Ins_Ptr (
    .Q(Ins_Ptr_q), .clk(Clock_out), .clr(Reset_out));  // open: load, D, count, carry
  Button Clock (.out(Clock_out));
  Button Reset (.out(Reset_out));
  ROM #(.addrWidth(4), .dataWidth(16)) rom_1 (
    .addr(Ins_Ptr_q), .data({Next_Instruction[15:8], lower_bits}));  // open: sel
  not not_1 (not_1_out, Next_Instruction[8]);
  not not_2 (not_2_out, Next_Instruction[9]);
  not not_3 (not_3_out, Next_Instruction[10]);
  not not_4 (not_4_out, Next_Instruction[14]);
  Multiplexer #(.width(8)) multiplexer_1 (
    .in0(sum), .in1(lower_bits), .out(multiplexer_1_out), .sel(MUX_select));  // open: en
  and mov (MUX_select, not_1_out, not_2_out, not_3_out, Next_Instruction[11], Next_Instruction[12], Next_Instruction[13], not_4_out, Next_Instruction[15]);
  Register rax (.D(multiplexer_1_out), .Q(rax_q), .clk(Clock_out), .clr(Reset_out));  // open: en
  Adder adder_1 (.a(rax_q), .b(lower_bits), .out(sum));  // open: cin, cout

  assign Next_Instruction[7:0] = lower_bits;

  // Notes on the sheet:
  //   Instruction Memory
  //   contents of rom_1 (hex, n*v repeats v):
  //   b802 8303 8304
endmodule
