// Logisim project Mulitiplier 4 bits.circ as structural Verilog: 1 circuit, main circuit main
module main (
  input  [3:0] Multiplicand,
  input  [3:0] Mulitiplier,
  output [7:0] Sum,
  output LSB,
  output [7:0] Product,
  output [7:0] Multiplicand__shifted
);

  wire Clk_out, Clock_out, Load_out;
  wire [7:0] multiplexer_1_out;

  Button Clock (.out(Clock_out));
  Button Load (.out(Load_out));
  or Clk (Clk_out, Load_out, Clock_out);
  Shift_Register Shifted (
    .in(1'b0), .clk(Clk_out), .load(Load_out), .d0(Multiplicand[0]), .q0(Multiplicand__shifted[0]),
    .d1(Multiplicand[1]), .q1(Multiplicand__shifted[1]), .d2(Multiplicand[2]), .q2(Multiplicand__shifted[2]),
    .d3(Multiplicand[3]), .q3(Multiplicand__shifted[3]), .d4(1'b0), .q4(Multiplicand__shifted[4]), .d5(1'b0),
    .q5(Multiplicand__shifted[5]), .d6(1'b0), .q6(Multiplicand__shifted[6]), .d7(1'b0),
    .q7(Multiplicand__shifted[7]));  // open: shift, out, clr
  Multiplexer #(.width(8)) multiplexer_1 (
    .in0({8{1'b0}}), .in1(Multiplicand__shifted), .out(multiplexer_1_out), .sel(LSB));  // open: en
  Shift_Register #(.length(4)) Shifted_2 (
    .in(1'b0), .clk(Clk_out), .load(Load_out), .d0(Mulitiplier[3]), .d1(Mulitiplier[2]), .d2(Mulitiplier[1]),
    .d3(Mulitiplier[0]), .q3(LSB));  // open: shift, out, clr, q0, q1, q2
  Register Register (.D(Sum), .Q(Product), .clk(Clk_out), .clr(Load_out));  // open: en
  Adder adder_1 (.a(multiplexer_1_out), .b(Product), .out(Sum));  // open: cin, cout

  // Notes on the sheet:
  //   Instructions:
  //   1. Set values for multiplicand and multiplier
  //   2. Click "Load" to initilize registers
  //   3. Click "Clock" to cycle through sequence
  //   4-bit Sequential Multiplier
endmodule
